# Fritzing sketch led_pong (saved by Fritzing 0.9.3b)
breadboards: 1

parts:
  LED_1 = LED - 5mm [color="Yellow (585nm)" package="5 mm [THT]"]
  R7 = Resistor [tolerance=±5% resistance=220 package=THT]
  POT_PIN = Rotary Potentiometer (Small) [maximum_resistance=10kΩ package=THT]
  R2 = Resistor [tolerance=±5% resistance=220 package=THT]
  R4 = Resistor [tolerance=±5% resistance=220 package=THT]
  T_2 = Pushbutton [package="[THT]"]
  T_3 = Pushbutton [package="[THT]"]
  LED_3 = LED - 5mm [color="Yellow (585nm)" package="5 mm [THT]"]
  T_1 = Pushbutton [package="[THT]"]
  R6 = Resistor [tolerance=±5% resistance=220 package=THT]
  LED_2 = LED - 5mm [color="Yellow (585nm)" package="5 mm [THT]"]
  R5 = Resistor [tolerance=±5% resistance=220 package=THT]
  LED_FLASH = LED - 5mm [color="Red (635nm)" package="5 mm [THT]"]
  R8 = Resistor [tolerance=±5% resistance=220 package=THT]
  Componente1 = Arduino Uno (Rev3)
  R3 = Resistor [tolerance=±5% resistance=220 package=THT]

nets:
  N1: LED_1.cathode, POT_PIN.leg1, R4.Pin_1, LED_3.cathode, LED_2.cathode, R5.Pin_1, LED_FLASH.cathode, Componente1.GND, R3.Pin_1
  N2: LED_1.anode, R6.Pin_1
  N3: R7.Pin_0, Componente1.D7
  N4: R7.Pin_1, LED_2.anode
  N5: POT_PIN.wiper, Componente1.A0
  N6: POT_PIN.leg2, T_2.Pin_3, T_2.Pin_4, T_3.Pin_3, T_3.Pin_4, T_1.Pin_3, T_1.Pin_4, Componente1.5V
  N7: R2.Pin_0, Componente1.D9_PWM
  N8: R2.Pin_1, LED_FLASH.anode
  N9: R4.Pin_0, T_1.Pin_1, T_1.Pin_2, Componente1.D2
  N10: T_2.Pin_1, T_2.Pin_2, R5.Pin_0, Componente1.D3_PWM
  N11: T_3.Pin_1, T_3.Pin_2, Componente1.D8, R3.Pin_0
  N12: LED_3.anode, R8.Pin_1
  N13: R6.Pin_0, Componente1.D5_PWM
  N14: R8.Pin_0, Componente1.D6_PWM
