# Fritzing sketch youngprogettino2 (saved by Fritzing 0.9.3b)
breadboards: 1

parts:
  Componente1 = Arduino Uno (Rev3)
  LED1 = LED - 5mm [color="Red (633nm)" package="5 mm [THT]"]
  LED2 = LED - 5mm [color="Red (633nm)" package="5 mm [THT]"]
  LED3 = LED - 5mm [color="Red (633nm)" package="5 mm [THT]"]
  T_1 = Pushbutton [package="[THT]"]
  POT = Rotary Potentiometer (Small) [maximum_resistance=100kΩ package=THT]
  DIST = HC-SR04 Ultrasonic Distance Sensor
  PIR = HC-SR501 Body Sensor Module
  R1 = Resistor [tolerance=±5% resistance=220 package=THT]
  R2 = Resistor [tolerance=±5% resistance=220 package=THT]
  R3 = Resistor [tolerance=±5% resistance=220 package=THT]
  RT_1 = Resistor [tolerance=±5% resistance=220 package=THT]

nets:
  N1: Componente1.A0, POT.wiper
  N2: Componente1.D8, DIST.TRIG
  N3: Componente1.D9_PWM, R1.Pin_1
  N4: Componente1.D10_PWM/SS, R2.Pin_1
  N5: Componente1.D11_PWM/MOSI, R3.Pin_1
  N6: Componente1.D2, PIR.OUT
  N7: Componente1.D4, T_1.Pin_3, T_1.Pin_4, RT_1.Pin_0
  N8: Componente1.D7, DIST.ECHO
  VCC: Componente1.5V, T_1.Pin_1, T_1.Pin_2, POT.leg2, DIST.VCC, PIR.VCC
  GND: Componente1.GND, POT.leg1, DIST.GND, PIR.GND, RT_1.Pin_1
  N9: LED1.anode, R1.Pin_0
  N10: LED2.anode, R2.Pin_0
  N11: LED3.anode, R3.Pin_0

custom parts:
  HC-SR501 Body Sensor Module: Pyroelectric Infrared PIR Motion Sensor Detector Module
